// Logisim project molor_basic_processor.circ as structural Verilog: 10 circuits, main circuit cpu
module cpu (
  input  [31:0] INST,
  input  CLK,
  input  [31:0] DOUT,
  input  [31:0] INC,
  input  RESET,
  input  [31:0] GPI,
  output [31:0] PC,
  output [31:0] MP,
  output [31:0] DIN,
  output WE,
  output [31:0] GPO
);

  wire and_1_out, and_2_out, and_3_out, and_4_out, and_5_out, and_6_out, and_7_out, and_8_out, and_9_out,
       and_10_out, and_11_out, and_12_out, and_13_out, and_14_out, comparator_1_eq, comparator_1_gt,
       comparator_1_lt, comparator_2_eq, comparator_2_gt, comparator_2_lt, multiplexer_2_out,
       multiplexer_17_out, nand_1_out, nor_1_out, not_1_out, or_1_out, or_2_out, or_3_out, or_4_out;
  wire [4:0] bit_extender_7_out;
  wire [7:0] bit_extender_6_out, bit_extender_16_out, bit_extender_19_out, multiplexer_6_out;
  wire [15:0] bit_extender_5_out, bit_extender_15_out, bit_extender_18_out, multiplexer_5_out;
  wire [23:0] bit_extender_4_out, bit_extender_14_out, bit_extender_17_out, multiplexer_4_out;
  wire [31:0] adder_1_out, adder_2_out, arithmetic_unit_1_o, bit_extender_1_out, bit_extender_2_out,
       bit_extender_3_out, bit_extender_8_out, bit_extender_9_out, bit_extender_10_out, bit_extender_11_out,
       bit_extender_12_out, bit_extender_13_out, bit_extender_20_out, logical_unit_1_o, multiplexer_1_out,
       multiplexer_3_out, multiplexer_7_out, multiplexer_8_out, multiplexer_9_out, multiplexer_10_out,
       multiplexer_11_out, multiplexer_12_out, multiplexer_13_out, multiplexer_14_out, multiplexer_15_out,
       multiplexer_16_out, multiplexer_18_out, multiplexer_20_out, multiplexer_21_out, register_memory_1_q1,
       register_memory_1_q2, register_memory_1_qd, shift_unit_1_o;

  and and_1 (and_1_out, ~INST[0], ~INST[1]);  // AND_Gate
  not not_1 (not_1_out, INST[2]);
  and and_2 (and_2_out, ~INST[0], INST[1]);  // AND_Gate
  and and_3 (and_3_out, INST[0], INST[1]);
  assign bit_extender_1_out = {{16{INST[23]}}, INST[23:8]};  // Bit_Extender bit_extender_1
  and and_4 (and_4_out, INST[4], and_1_out);
  and and_5 (and_5_out, and_1_out, ~INST[4]);  // AND_Gate
  nand nand_1 (nand_1_out, and_3_out, INST[31]);
  and and_6 (and_6_out, ~INST[3], INST[2]);  // AND_Gate
  Multiplexer #(.width(32)) multiplexer_1 (
    .in0(register_memory_1_q2), .in1(bit_extender_1_out), .out(multiplexer_1_out), .sel(INST[2]));
  assign bit_extender_2_out = {{16{1'b0}}, INST[23:8]};  // Bit_Extender bit_extender_2
  assign bit_extender_3_out = {{16{INST[23]}}, INST[23:8]};  // Bit_Extender bit_extender_3
  Bit_Extender #(.in_width(32), .out_width(24), .\type ("zero")) bit_extender_4 (.in(DOUT), .out(bit_extender_4_out));
  Bit_Extender #(.in_width(32), .\type ("zero")) bit_extender_5 (.in(DOUT), .out(bit_extender_5_out));
  Bit_Extender #(.in_width(32), .out_width(8), .\type ("zero")) bit_extender_6 (.in(DOUT), .out(bit_extender_6_out));
  Multiplexer #(.select(2)) multiplexer_2 (
    .in0(1'b1), .in1(not_1_out), .in2(or_3_out), .in3(and_6_out), .out(multiplexer_2_out), .sel(INST[1:0]));
  Bit_Extender #(.in_width(32), .out_width(5), .\type ("zero")) bit_extender_7 (
    .in(multiplexer_1_out), .out(bit_extender_7_out));
  Multiplexer #(.width(32)) multiplexer_3 (
    .in0(bit_extender_2_out), .in1(bit_extender_3_out), .out(multiplexer_3_out), .sel(INST[6]));
  assign bit_extender_8_out = {{8{1'b0}}, bit_extender_4_out};  // Bit_Extender bit_extender_8
  assign bit_extender_9_out = {{16{1'b0}}, bit_extender_5_out};  // Bit_Extender bit_extender_9
  assign bit_extender_10_out = {{24{1'b0}}, bit_extender_6_out};  // Bit_Extender bit_extender_10
  assign bit_extender_11_out = {{8{bit_extender_4_out[23]}}, bit_extender_4_out};  // Bit_Extender bit_extender_11
  assign bit_extender_12_out = {{16{bit_extender_5_out[15]}}, bit_extender_5_out};  // Bit_Extender bit_extender_12
  assign bit_extender_13_out = {{24{bit_extender_6_out[7]}}, bit_extender_6_out};  // Bit_Extender bit_extender_13
  Bit_Extender #(.in_width(32), .out_width(24), .\type ("zero")) bit_extender_14 (
    .in(register_memory_1_qd), .out(bit_extender_14_out));
  Multiplexer #(.width(24)) multiplexer_4 (
    .in0(bit_extender_14_out), .in1(bit_extender_17_out), .out(multiplexer_4_out), .sel(INST[6]));
  Bit_Extender #(.in_width(32), .\type ("zero")) bit_extender_15 (.in(register_memory_1_qd), .out(bit_extender_15_out));
  Multiplexer #(.width(16)) multiplexer_5 (
    .in0(bit_extender_15_out), .in1(bit_extender_18_out), .out(multiplexer_5_out), .sel(INST[6]));
  Bit_Extender #(.in_width(32), .out_width(8), .\type ("zero")) bit_extender_16 (
    .in(register_memory_1_qd), .out(bit_extender_16_out));
  Multiplexer #(.width(8)) multiplexer_6 (
    .in0(bit_extender_16_out), .in1(bit_extender_19_out), .out(multiplexer_6_out), .sel(INST[6]));
  Bit_Extender #(.in_width(32), .out_width(24)) bit_extender_17 (.in(register_memory_1_qd), .out(bit_extender_17_out));
  Bit_Extender #(.in_width(32)) bit_extender_18 (.in(register_memory_1_qd), .out(bit_extender_18_out));
  Bit_Extender #(.in_width(32), .out_width(8)) bit_extender_19 (.in(register_memory_1_qd), .out(bit_extender_19_out));
  Multiplexer #(.width(32)) multiplexer_7 (
    .in0(register_memory_1_qd), .in1(multiplexer_15_out), .out(multiplexer_7_out), .sel(INST[5]));
  Multiplexer #(.width(32)) multiplexer_8 (
    .in0(adder_2_out), .in1(bit_extender_20_out), .out(multiplexer_8_out), .sel(INST[5]));
  Multiplexer #(.select(2), .width(32)) multiplexer_9 (
    .in0(multiplexer_16_out), .in1(multiplexer_18_out), .in2(multiplexer_8_out), .in3(GPI),
    .out(multiplexer_9_out), .sel(INST[1:0]));
  Multiplexer #(.width(32)) multiplexer_10 (
    .in0(bit_extender_8_out), .in1(bit_extender_11_out), .out(multiplexer_10_out), .sel(INST[6]));
  Multiplexer #(.width(32)) multiplexer_11 (
    .in0(bit_extender_9_out), .in1(bit_extender_12_out), .out(multiplexer_11_out), .sel(INST[6]));
  Multiplexer #(.width(32)) multiplexer_12 (
    .in0(bit_extender_10_out), .in1(bit_extender_13_out), .out(multiplexer_12_out), .sel(INST[6]));
  and and_7 (and_7_out, INST[2], comparator_1_gt);
  Comparator #(.mode("unsigned"), .width(32)) comparator_1 (
    .a(register_memory_1_q1), .b(multiplexer_7_out), .gt(comparator_1_gt), .eq(comparator_1_eq),
    .lt(comparator_1_lt));
  and and_8 (and_8_out, INST[2], comparator_2_gt);
  Comparator #(.width(32)) comparator_2 (
    .a(register_memory_1_q1), .b(multiplexer_7_out), .gt(comparator_2_gt), .eq(comparator_2_eq),
    .lt(comparator_2_lt));
  Multiplexer #(.select(2), .width(32)) multiplexer_13 (
    .in0(DOUT), .in1(multiplexer_10_out), .in2(multiplexer_11_out), .in3(multiplexer_12_out),
    .out(multiplexer_13_out), .sel(INST[5:4]));
  and and_9 (and_9_out, INST[3], comparator_1_eq);
  and and_10 (and_10_out, INST[3], comparator_2_eq);
  shift_unit shift_unit_1 (
    .A(register_memory_1_q1), .DIST(bit_extender_7_out), .DIRECTION(INST[5]), .ARITHMETIC(INST[7]),
    .CARRY(INST[6]), .CLOCK(CLK), .WE(and_4_out), .RESET(RESET), .O(shift_unit_1_o));
  Multiplexer #(.width(32)) multiplexer_14 (
    .in0(arithmetic_unit_1_o), .in1(shift_unit_1_o), .out(multiplexer_14_out), .sel(INST[4]));
  arithmetic_unit arithmetic_unit_1 (
    .A(register_memory_1_q1), .B(multiplexer_1_out), .CARRY(INST[6]), .NEGATE(INST[5]), .CLOCK(CLK),
    .RESET(RESET), .WE(and_5_out), .O(arithmetic_unit_1_o));
  logical_unit logical_unit_1 (
    .A(register_memory_1_q1), .B(multiplexer_1_out), .GATE_IDX(INST[5:4]), .O(logical_unit_1_o));
  Multiplexer #(.width(32)) multiplexer_15 (
    .in0(register_memory_1_q2), .in1(bit_extender_1_out), .out(multiplexer_15_out), .sel(INST[6]));
  nor nor_1 (nor_1_out, INST[2], INST[3], INST[4]);
  or or_1 (or_1_out, and_7_out, and_9_out, and_11_out);
  and and_11 (and_11_out, INST[4], comparator_1_lt);
  or or_2 (or_2_out, and_8_out, and_10_out, and_12_out);
  and and_12 (and_12_out, INST[4], comparator_2_lt);
  Multiplexer #(.width(32)) multiplexer_16 (
    .in0(multiplexer_14_out), .in1(logical_unit_1_o), .out(multiplexer_16_out), .sel(INST[3]));
  or or_3 (or_3_out, nor_1_out, INST[5]);
  Multiplexer multiplexer_17 (.in0(or_1_out), .in1(or_2_out), .out(multiplexer_17_out), .sel(INST[7]));
  Multiplexer #(.width(32)) multiplexer_18 (
    .in0(multiplexer_3_out), .in1(multiplexer_13_out), .out(multiplexer_18_out), .sel(INST[3]));
  Multiplexer #(.select(2), .width(32)) multiplexer_19 (
    .in0(register_memory_1_qd), .in1({DOUT[31:24], multiplexer_4_out}),
    .in2({DOUT[31:16], multiplexer_5_out}), .in3({DOUT[31:8], multiplexer_6_out}), .out(DIN), .sel(INST[5:4]));
  Multiplexer #(.width(32)) multiplexer_20 (
    .in0(PC), .in1(register_memory_1_q1), .out(multiplexer_20_out), .sel(INST[6]));
  register_memory register_memory_1 (
    .RS1(INST[27:24]), .RS2(INST[23:20]), .RD(INST[31:28]), .DATA(multiplexer_9_out), .WE(multiplexer_2_out),
    .CLK(CLK), .RST(RESET), .Q1(register_memory_1_q1), .Q2(register_memory_1_q2), .QD(register_memory_1_qd));
  Adder #(.width(32)) adder_1 (.a(multiplexer_20_out), .b(bit_extender_1_out), .out(adder_1_out));  // open: cin, cout
  assign bit_extender_20_out = {{31{1'b0}}, multiplexer_17_out};  // Bit_Extender bit_extender_20
  or or_4 (or_4_out, nor_1_out, multiplexer_17_out);
  and and_13 (and_13_out, INST[2], INST[3]);
  and and_14 (and_14_out, ~INST[5], and_2_out, or_4_out);  // AND_Gate
  Register #(.trigger("falling"), .width(32)) PROG_CTR (
    .D(multiplexer_21_out), .en(nand_1_out), .clk(CLK), .Q(PC), .clr(RESET));
  Multiplexer #(.width(32)) multiplexer_21 (
    .in0(adder_2_out), .in1(adder_1_out), .out(multiplexer_21_out), .sel(and_14_out));
  Register #(.width(32)) register_1 (.D(register_memory_1_q1), .en(and_13_out), .clk(CLK), .Q(GPO), .clr(RESET));
  Adder #(.width(32)) adder_2 (.a(PC), .b(INC), .out(adder_2_out));  // open: cin, cout
  and and_15 (WE, INST[2], INST[0], ~INST[1]);  // AND_Gate
  Adder #(.width(32)) adder_3 (.a(register_memory_1_q1), .b(bit_extender_1_out), .out(MP));  // open: cin, cout
endmodule

module register_memory (
  input  [3:0] RS1,
  input  [3:0] RS2,
  input  [3:0] RD,
  input  [31:0] DATA,
  input  WE,
  input  CLK,
  input  RST,
  output [31:0] Q1,
  output [31:0] Q2,
  output [31:0] QD
);

  wire demultiplexer_1_out0, demultiplexer_1_out1, demultiplexer_1_out2, demultiplexer_1_out3,
       demultiplexer_1_out4, demultiplexer_1_out5, demultiplexer_1_out6, demultiplexer_1_out7,
       demultiplexer_1_out8, demultiplexer_1_out9, demultiplexer_1_out10, demultiplexer_1_out11,
       demultiplexer_1_out12, demultiplexer_1_out13, demultiplexer_1_out14;
  wire [31:0] register_1_q, register_2_q, register_3_q, register_4_q, register_5_q, register_6_q,
       register_7_q, register_8_q, register_9_q, register_10_q, register_11_q, register_12_q, register_13_q,
       register_14_q, register_15_q;

  Demultiplexer #(.select(4)) demultiplexer_1 (
    .out0(demultiplexer_1_out0), .out1(demultiplexer_1_out1), .out2(demultiplexer_1_out2),
    .out3(demultiplexer_1_out3), .out4(demultiplexer_1_out4), .out5(demultiplexer_1_out5),
    .out6(demultiplexer_1_out6), .out7(demultiplexer_1_out7), .out8(demultiplexer_1_out8),
    .out9(demultiplexer_1_out9), .out10(demultiplexer_1_out10), .out11(demultiplexer_1_out11),
    .out12(demultiplexer_1_out12), .out13(demultiplexer_1_out13), .out14(demultiplexer_1_out14), .in(CLK),
    .sel(RD));  // open: out15
  Register #(.width(32)) register_1 (.D(DATA), .en(WE), .clk(demultiplexer_1_out0), .Q(register_1_q), .clr(RST));
  Register #(.width(32)) register_2 (.D(DATA), .en(WE), .clk(demultiplexer_1_out1), .Q(register_2_q), .clr(RST));
  Register #(.width(32)) register_3 (.D(DATA), .en(WE), .clk(demultiplexer_1_out2), .Q(register_3_q), .clr(RST));
  Register #(.width(32)) register_4 (.D(DATA), .en(WE), .clk(demultiplexer_1_out3), .Q(register_4_q), .clr(RST));
  Register #(.width(32)) register_5 (.D(DATA), .en(WE), .clk(demultiplexer_1_out4), .Q(register_5_q), .clr(RST));
  Register #(.width(32)) register_6 (.D(DATA), .en(WE), .clk(demultiplexer_1_out5), .Q(register_6_q), .clr(RST));
  Register #(.width(32)) register_7 (.D(DATA), .en(WE), .clk(demultiplexer_1_out6), .Q(register_7_q), .clr(RST));
  Register #(.width(32)) register_8 (.D(DATA), .en(WE), .clk(demultiplexer_1_out7), .Q(register_8_q), .clr(RST));
  Register #(.width(32)) register_9 (.D(DATA), .en(WE), .clk(demultiplexer_1_out8), .Q(register_9_q), .clr(RST));
  Register #(.width(32)) register_10 (.D(DATA), .en(WE), .clk(demultiplexer_1_out9), .Q(register_10_q), .clr(RST));
  Register #(.width(32)) register_11 (.D(DATA), .en(WE), .clk(demultiplexer_1_out10), .Q(register_11_q), .clr(RST));
  Register #(.width(32)) register_12 (.D(DATA), .en(WE), .clk(demultiplexer_1_out11), .Q(register_12_q), .clr(RST));
  Register #(.width(32)) register_13 (.D(DATA), .en(WE), .clk(demultiplexer_1_out12), .Q(register_13_q), .clr(RST));
  Register #(.width(32)) register_14 (.D(DATA), .en(WE), .clk(demultiplexer_1_out13), .Q(register_14_q), .clr(RST));
  Register #(.width(32)) register_15 (.D(DATA), .en(WE), .clk(demultiplexer_1_out14), .Q(register_15_q), .clr(RST));
  Multiplexer #(.select(4), .width(32)) multiplexer_1 (
    .in0(register_1_q), .in1(register_2_q), .in2(register_3_q), .in3(register_4_q), .in4(register_5_q),
    .in5(register_6_q), .in6(register_7_q), .in7(register_8_q), .in8(register_9_q), .in9(register_10_q),
    .in10(register_11_q), .in11(register_12_q), .in12(register_13_q), .in13(register_14_q),
    .in14(register_15_q), .in15({32{1'b0}}), .out(Q1), .sel(RS1));
  Multiplexer #(.select(4), .width(32)) multiplexer_2 (
    .in0(register_1_q), .in1(register_2_q), .in2(register_3_q), .in3(register_4_q), .in4(register_5_q),
    .in5(register_6_q), .in6(register_7_q), .in7(register_8_q), .in8(register_9_q), .in9(register_10_q),
    .in10(register_11_q), .in11(register_12_q), .in12(register_13_q), .in13(register_14_q),
    .in14(register_15_q), .in15({32{1'b0}}), .out(Q2), .sel(RS2));
  Multiplexer #(.select(4), .width(32)) multiplexer_3 (
    .in0(register_1_q), .in1(register_2_q), .in2(register_3_q), .in3(register_4_q), .in4(register_5_q),
    .in5(register_6_q), .in6(register_7_q), .in7(register_8_q), .in8(register_9_q), .in9(register_10_q),
    .in10(register_11_q), .in11(register_12_q), .in12(register_13_q), .in13(register_14_q),
    .in14(register_15_q), .in15({32{1'b0}}), .out(QD), .sel(RD));
endmodule

module main (
  input  in_1
);

  wire clock_1_out, cpu_1_we;
  wire [15:0] bit_extender_1_out, bit_extender_2_out;
  wire [31:0] cpu_1_din, cpu_1_mp, cpu_1_pc, memory64kx8_1_dout, rom_1_data;

  Clock clock_1 (.out(clock_1_out));
  Bit_Extender #(.in_width(32)) bit_extender_1 (.in(cpu_1_pc), .out(bit_extender_1_out));
  ROM #(.addrWidth(16), .dataWidth(32)) rom_1 (.addr(bit_extender_1_out), .data(rom_1_data));
  memory64kx8 memory64kx8_1 (
    .ADDR(bit_extender_2_out), .WE(cpu_1_we), .CLK(clock_1_out), .DIN(cpu_1_din), .DOUT(memory64kx8_1_dout));
  cpu cpu_1 (
    .INST(rom_1_data), .CLK(clock_1_out), .DOUT(memory64kx8_1_dout), .INC(32'h1), .RESET(in_1),
    .PC(cpu_1_pc), .MP(cpu_1_mp), .DIN(cpu_1_din), .WE(cpu_1_we));  // open: GPI, GPO
  Bit_Extender #(.in_width(32), .\type ("zero")) bit_extender_2 (.in(cpu_1_mp), .out(bit_extender_2_out));

  // Notes on the sheet:
  //   contents of rom_1 (hex, n*v repeats v):
  //   800001 1014 118 f 400001 1014 218 f 200001 1014 418 f 100001 1014 818 f 80001 1014 1018 f 40001 1014
  //   2018 f 20001 1014 4018 f 10001 1014 8018 f 8001 1014 10018 f 4001 1014 20018 f 2001 1014 40018 f
  //   1001 1014 80018 f 801 1014 100018 f 401 1014 200018 f 201 1014 400018 f 101 1014 800018 f f00005e
endmodule

module memory64kx8 (
  input  [15:0] ADDR,
  input  WE,
  input  CLK,
  input  [31:0] DIN,
  output [31:0] DOUT
);

  wire comparator_1_lt, comparator_2_lt, comparator_3_lt, not_1_out, not_2_out, not_3_out;
  wire [7:0] multiplexer_1_out, multiplexer_2_out, multiplexer_3_out, multiplexer_4_out, ram_1_dout,
       ram_2_dout, ram_3_dout, ram_4_dout;
  wire [13:0] adder_1_out, adder_2_out, adder_3_out;

  Multiplexer #(.select(2), .width(8)) multiplexer_1 (
    .in0(DIN[7:0]), .in1(DIN[31:24]), .in2(DIN[23:16]), .in3(DIN[15:8]), .out(multiplexer_1_out),
    .sel(ADDR[1:0]));
  Multiplexer #(.select(2), .width(8)) multiplexer_2 (
    .in0(DIN[15:8]), .in1(DIN[7:0]), .in2(DIN[31:24]), .in3(DIN[23:16]), .out(multiplexer_2_out),
    .sel(ADDR[1:0]));
  Multiplexer #(.select(2), .width(8)) multiplexer_3 (
    .in0(DIN[23:16]), .in1(DIN[15:8]), .in2(DIN[7:0]), .in3(DIN[31:24]), .out(multiplexer_3_out),
    .sel(ADDR[1:0]));
  Multiplexer #(.select(2), .width(8)) multiplexer_4 (
    .in0(DIN[31:24]), .in1(DIN[23:16]), .in2(DIN[15:8]), .in3(DIN[7:0]), .out(multiplexer_4_out),
    .sel(ADDR[1:0]));
  Comparator #(.mode("unsigned"), .width(2)) comparator_1 (
    .a(ADDR[1:0]), .b(2'b01), .lt(comparator_1_lt));  // open: gt, eq
  not not_1 (not_1_out, comparator_1_lt);
  Comparator #(.mode("unsigned"), .width(2)) comparator_2 (
    .a(ADDR[1:0]), .b(2'b10), .lt(comparator_2_lt));  // open: gt, eq
  not not_2 (not_2_out, comparator_2_lt);
  Comparator #(.mode("unsigned"), .width(2)) comparator_3 (
    .a(ADDR[1:0]), .b(2'b11), .lt(comparator_3_lt));  // open: gt, eq
  not not_3 (not_3_out, comparator_3_lt);
  Adder #(.width(14)) adder_1 (.a(ADDR[15:2]), .b({14{1'b0}}), .out(adder_1_out), .cin(not_2_out));  // open: cout
  RAM #(.addrWidth(14), .enables("line")) ram_1 (
    .addr(adder_2_out), .we(WE), .clk(CLK), .din(multiplexer_1_out), .dout(ram_1_dout));
  Adder #(.width(14)) adder_2 (.a(ADDR[15:2]), .b({14{1'b0}}), .out(adder_2_out), .cin(not_1_out));  // open: cout
  RAM #(.addrWidth(14), .enables("line")) ram_2 (
    .addr(adder_1_out), .we(WE), .clk(CLK), .din(multiplexer_2_out), .dout(ram_2_dout));
  RAM #(.addrWidth(14), .enables("line")) ram_3 (
    .addr(adder_3_out), .we(WE), .clk(CLK), .din(multiplexer_3_out), .dout(ram_3_dout));
  Adder #(.width(14)) adder_3 (.a(ADDR[15:2]), .b({14{1'b0}}), .out(adder_3_out), .cin(not_3_out));  // open: cout
  RAM #(.addrWidth(14), .enables("line")) ram_4 (
    .addr(ADDR[15:2]), .we(WE), .clk(CLK), .din(multiplexer_4_out), .dout(ram_4_dout));
  Multiplexer #(.select(2), .width(8)) multiplexer_5 (
    .in0(ram_1_dout), .in1(ram_2_dout), .in2(ram_3_dout), .in3(ram_4_dout), .out(DOUT[7:0]), .sel(ADDR[1:0]));
  Multiplexer #(.select(2), .width(8)) multiplexer_6 (
    .in0(ram_2_dout), .in1(ram_3_dout), .in2(ram_4_dout), .in3(ram_1_dout), .out(DOUT[15:8]), .sel(ADDR[1:0]));
  Multiplexer #(.select(2), .width(8)) multiplexer_7 (
    .in0(ram_3_dout), .in1(ram_4_dout), .in2(ram_1_dout), .in3(ram_2_dout), .out(DOUT[23:16]), .sel(ADDR[1:0]));
  Multiplexer #(.select(2), .width(8)) multiplexer_8 (
    .in0(ram_4_dout), .in1(ram_1_dout), .in2(ram_2_dout), .in3(ram_3_dout), .out(DOUT[31:24]), .sel(ADDR[1:0]));
endmodule

module shift_unit (
  input  [31:0] A,
  input  [4:0] DIST,
  input  DIRECTION,
  input  ARITHMETIC,
  input  CARRY,
  input  CLOCK,
  input  WE,
  input  RESET,
  output [31:0] O
);

  wire and_1_out, and_2_out;
  wire [31:0] bit_extender_1_out, left_shift32bit_1_cout, left_shift32bit_1_o, multiplexer_1_out,
       multiplexer_2_out, multiplexer_3_out, register_1_q, register_2_q, right_shift32bit_1_cout,
       right_shift32bit_1_o;

  assign bit_extender_1_out = {{31{A[31]}}, A[31]};  // Bit_Extender bit_extender_1
  Multiplexer #(.width(32)) multiplexer_1 (
    .in0(multiplexer_3_out), .in1(bit_extender_1_out), .out(multiplexer_1_out), .sel(ARITHMETIC));
  Register #(.width(32)) register_1 (
    .D(left_shift32bit_1_cout), .en(and_1_out), .clk(CLOCK), .Q(register_1_q), .clr(RESET));
  and and_1 (and_1_out, ~DIRECTION, WE);  // AND_Gate
  Register #(.width(32)) register_2 (
    .D(right_shift32bit_1_cout), .en(and_2_out), .clk(CLOCK), .Q(register_2_q), .clr(RESET));
  Multiplexer #(.width(32)) multiplexer_2 (.in0({32{1'b0}}), .in1(register_1_q), .out(multiplexer_2_out), .sel(CARRY));
  and and_2 (and_2_out, DIRECTION, WE);
  left_shift32bit left_shift32bit_1 (
    .DIST(DIST), .Cin(multiplexer_2_out), .A(A), .Cout(left_shift32bit_1_cout), .O(left_shift32bit_1_o));
  right_shift32bit right_shift32bit_1 (
    .A(A), .Cin(multiplexer_1_out), .DIST(DIST), .O(right_shift32bit_1_o), .Cout(right_shift32bit_1_cout));
  Multiplexer #(.width(32)) multiplexer_3 (.in0({32{1'b0}}), .in1(register_2_q), .out(multiplexer_3_out), .sel(CARRY));
  Multiplexer #(.width(32)) multiplexer_4 (
    .in0(left_shift32bit_1_o), .in1(right_shift32bit_1_o), .out(O), .sel(DIRECTION));
endmodule

module arithmetic_unit (
  input  [31:0] A,
  input  [31:0] B,
  input  CARRY,
  input  NEGATE,
  input  CLOCK,
  input  RESET,
  input  WE,
  output [31:0] O
);

  wire adder_1_cout, and_1_out, and_2_out, and_3_out, and_4_out, register_1_q, register_2_q,
       subtractor_1_bout;
  wire [31:0] adder_1_out, subtractor_1_out;

  and and_1 (and_1_out, CARRY, register_1_q);
  and and_2 (and_2_out, CARRY, register_2_q);
  and and_3 (and_3_out, ~NEGATE, WE);  // AND_Gate
  Adder #(.width(32)) adder_1 (.a(A), .b(B), .out(adder_1_out), .cin(and_1_out), .cout(adder_1_cout));
  Subtractor #(.width(32)) subtractor_1 (
    .a(A), .b(B), .out(subtractor_1_out), .bin(and_2_out), .bout(subtractor_1_bout));
  Register #(.width(1)) register_1 (.D(adder_1_cout), .en(and_3_out), .clk(CLOCK), .Q(register_1_q), .clr(RESET));
  Register #(.width(1)) register_2 (.D(subtractor_1_bout), .en(and_4_out), .clk(CLOCK), .Q(register_2_q), .clr(RESET));
  and and_4 (and_4_out, NEGATE, WE);
  Multiplexer #(.width(32)) multiplexer_1 (.in0(adder_1_out), .in1(subtractor_1_out), .out(O), .sel(NEGATE));
endmodule

module logical_unit (
  input  [31:0] A,
  input  [31:0] B,
  input  [1:0] GATE_IDX,
  output [31:0] O
);

  wire [31:0] and_1_out, not_1_out, or_1_out, xor_1_out;

  assign and_1_out = A & B;  // AND_Gate and_1, 32 bits wide
  assign or_1_out = A | B;  // OR_Gate or_1, 32 bits wide
  assign xor_1_out = A ^ B;  // XOR_Gate xor_1, 32 bits wide
  assign not_1_out = ~A;  // NOT_Gate not_1, 32 bits wide
  Multiplexer #(.select(2), .width(32)) multiplexer_1 (
    .in0(and_1_out), .in1(or_1_out), .in2(xor_1_out), .in3(not_1_out), .out(O), .sel(GATE_IDX));
endmodule

module left_shift32bit (
  input  [4:0] DIST,
  input  [31:0] Cin,
  input  [31:0] A,
  output [31:0] Cout,
  output [31:0] O
);

  wire [15:0] multiplexer_7_out, multiplexer_8_out_2;
  wire [31:0] multiplexer_1_out, multiplexer_2_out, multiplexer_3_out, multiplexer_4_out, multiplexer_5_out,
       multiplexer_6_out, multiplexer_8_out;

  Multiplexer #(.width(32)) multiplexer_1 (
    .in0(Cin), .in1({{31{1'b0}}, A[31]}), .out(multiplexer_1_out), .sel(DIST[0]));
  Multiplexer #(.width(32)) multiplexer_2 (.in0(A), .in1({A[30:0], Cin[31]}), .out(multiplexer_2_out), .sel(DIST[0]));
  Multiplexer #(.width(32)) multiplexer_3 (
    .in0(multiplexer_1_out), .in1({{30{1'b0}}, multiplexer_2_out[31:30]}), .out(multiplexer_3_out),
    .sel(DIST[1]));
  Multiplexer #(.width(32)) multiplexer_4 (
    .in0(multiplexer_2_out), .in1({multiplexer_2_out[29:0], multiplexer_1_out[31:30]}),
    .out(multiplexer_4_out), .sel(DIST[1]));
  Multiplexer #(.width(32)) multiplexer_5 (
    .in0(multiplexer_3_out), .in1({{28{1'b0}}, multiplexer_4_out[31:28]}), .out(multiplexer_5_out),
    .sel(DIST[2]));
  Multiplexer #(.width(32)) multiplexer_6 (
    .in0(multiplexer_4_out), .in1({multiplexer_4_out[27:0], multiplexer_3_out[31:28]}),
    .out(multiplexer_6_out), .sel(DIST[2]));
  Multiplexer #(.width(32)) multiplexer_7 (
    .in0(multiplexer_5_out), .in1({{24{1'b0}}, multiplexer_6_out[31:24]}),
    .out({multiplexer_8_out[15:0], multiplexer_7_out}), .sel(DIST[3]));
  Multiplexer #(.width(32)) multiplexer_8 (
    .in0(multiplexer_6_out), .in1({multiplexer_6_out[23:0], multiplexer_5_out[31:24]}),
    .out({multiplexer_8_out_2, multiplexer_8_out[31:16]}), .sel(DIST[3]));
  Multiplexer #(.width(32)) multiplexer_9 (
    .in0({multiplexer_8_out[15:0], multiplexer_7_out}), .in1({{16{1'b0}}, multiplexer_8_out_2}), .out(Cout),
    .sel(DIST[4]));
  Multiplexer #(.width(32)) multiplexer_10 (
    .in0({multiplexer_8_out_2, multiplexer_8_out[31:16]}), .in1(multiplexer_8_out), .out(O), .sel(DIST[4]));
endmodule

module right_shift32bit (
  input  [31:0] A,
  input  [31:0] Cin,
  input  [4:0] DIST,
  output [31:0] O,
  output [31:0] Cout
);

  wire [31:0] multiplexer_1_out_2, multiplexer_3_out_2, multiplexer_5_out_2, multiplexer_7_out_2;
  wire [31:2] multiplexer_2_out;
  wire [31:4] multiplexer_4_out;
  wire [31:8] multiplexer_6_out;
  wire [31:16] multiplexer_7_out, multiplexer_8_out;
  wire [31:24] multiplexer_5_out;
  wire [31:28] multiplexer_3_out;
  wire [31:30] multiplexer_1_out;

  Multiplexer #(.width(32)) multiplexer_1 (
    .in0(A), .in1({Cin[0], A[31:1]}), .out({multiplexer_1_out_2[29:0], multiplexer_1_out}), .sel(DIST[0]));
  Multiplexer #(.width(32)) multiplexer_2 (
    .in0(Cin), .in1({A[0], {31{1'b0}}}), .out({multiplexer_2_out, multiplexer_1_out_2[31:30]}), .sel(DIST[0]));
  Multiplexer #(.width(32)) multiplexer_3 (
    .in0({multiplexer_1_out_2[29:0], multiplexer_1_out}), .in1(multiplexer_1_out_2),
    .out({multiplexer_3_out_2[27:0], multiplexer_3_out}), .sel(DIST[1]));
  Multiplexer #(.width(32)) multiplexer_4 (
    .in0({multiplexer_2_out, multiplexer_1_out_2[31:30]}), .in1({multiplexer_1_out, {30{1'b0}}}),
    .out({multiplexer_4_out, multiplexer_3_out_2[31:28]}), .sel(DIST[1]));
  Multiplexer #(.width(32)) multiplexer_5 (
    .in0({multiplexer_3_out_2[27:0], multiplexer_3_out}), .in1(multiplexer_3_out_2),
    .out({multiplexer_5_out_2[23:0], multiplexer_5_out}), .sel(DIST[2]));
  Multiplexer #(.width(32)) multiplexer_6 (
    .in0({multiplexer_4_out, multiplexer_3_out_2[31:28]}), .in1({multiplexer_3_out, {28{1'b0}}}),
    .out({multiplexer_6_out, multiplexer_5_out_2[31:24]}), .sel(DIST[2]));
  Multiplexer #(.width(32)) multiplexer_7 (
    .in0({multiplexer_5_out_2[23:0], multiplexer_5_out}), .in1(multiplexer_5_out_2),
    .out({multiplexer_7_out_2[15:0], multiplexer_7_out}), .sel(DIST[3]));
  Multiplexer #(.width(32)) multiplexer_8 (
    .in0({multiplexer_6_out, multiplexer_5_out_2[31:24]}), .in1({multiplexer_5_out, {24{1'b0}}}),
    .out({multiplexer_8_out, multiplexer_7_out_2[31:16]}), .sel(DIST[3]));
  Multiplexer #(.width(32)) multiplexer_9 (
    .in0({multiplexer_7_out_2[15:0], multiplexer_7_out}), .in1(multiplexer_7_out_2), .out(O), .sel(DIST[4]));
  Multiplexer #(.width(32)) multiplexer_10 (
    .in0({multiplexer_8_out, multiplexer_7_out_2[31:16]}), .in1({multiplexer_7_out, {16{1'b0}}}), .out(Cout),
    .sel(DIST[4]));
endmodule

module bad_apple (
);

  wire clock_1_out;
  wire [15:0] bit_extender_1_out;
  wire [31:0] cpu_1_gpo, cpu_1_pc, rom_1_data;

  Bit_Extender #(.in_width(32), .\type ("zero")) bit_extender_1 (.in(cpu_1_pc), .out(bit_extender_1_out));
  ROM #(.addrWidth(16), .dataWidth(32)) rom_1 (.addr(bit_extender_1_out), .data(rom_1_data));
  Clock clock_1 (.out(clock_1_out));
  cpu cpu_1 (
    .INST(rom_1_data), .CLK(clock_1_out), .INC(32'h1), .PC(cpu_1_pc), .GPO(cpu_1_gpo));  // open: DOUT, RESET, GPI, MP, DIN, WE
  // DotMatrix #(.dotshape("circle"), .inputtype("select"), .matrixcols(16), .matrixrows(16)) dotmatrix_1: pin names not known; wires that end beside it: cpu_1_gpo[15:0], cpu_1_gpo[31:16]

  // Notes on the sheet:
  //   contents of rom_1 (hex, n*v repeats v):
  //   800001 1014 118 f 400001 1014 218 f 200001 1014 418 f 100001 1014 818 f 80001 1014 1018 f 40001 1014
  //   2018 f 20001 1014 4018 f 10001 1014 8018 f 8001 1014 10018 f 4001 1014 20018 f 2001 1014 40018 f
  //   1001 1014 80018 f 801 1014 100018 f 401 1014 200018 f 201 1014 400018 f 101 1014 800018 f f00005e
endmodule
